# Fritzing sketch betterU_blob (saved by Fritzing 0.9.0b)
breadboards: 1

parts:
  Part1 = Arduino Uno (Rev3)
  neopixel1 = Neopixel Ring 12
  Part2 = JY-MCU
  R1 = Resistor [tolerance=±5% resistance=220 package=THT]
  R2 = Resistor [tolerance=±5% resistance=220 package=THT]

nets:
  N1: Part1.D10_PWM/SS, Part2.TX
  N2: Part1.D11_PWM/MOSI, R1.Pin_0
  GND: Part1.GND, neopixel1.GND, Part2.GND
  N3: Part1.D6_PWM, neopixel1.IN
  3V3: Part1.3V3, Part2.VCC
  5V: Part1.5V, neopixel1.VCC
  N4: Part2.RX, R1.Pin_1, R2.Pin_0

custom parts:
  Neopixel Ring 12: Neopixel Ring x12
  JY-MCU: Description: The Bluetooth Mate is very similar to our BlueSMiRF modem, but it is designed specifically to be used with our Arduino Pros and LilyPad Arduinos. These modems work as a serial (RX/TX) pipe, and are a great wireless replacement for serial cables. Any serial stream from 9600 to 115200bps can be passed seamlessly from your computer to your target. Bluetooth Mate has the same pin out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
